// Logisim project CC.circ as structural Verilog: 1 circuit, main circuit CC
module CC (
  input  [3:0] icode,
  input  [3:0] ifun,
  input  Clock,
  input  Reset,
  input  ZF,
  input  SF,
  input  OF,
  output [2:0] CC,
  output CC_true,
  output invalid_ifun
);

  wire and_1_out, main_1__0, main_1__1, main_1__2, main_1__3, main_1__4, main_1__5, main_1__6, main_1__7,
       multiplexer_1_out;

  Multiplexer #(.select(4)) multiplexer_1 (
    .in0(1'b0), .in1(1'b0), .in2(1'b0), .in3(1'b0), .in4(1'b0), .in5(1'b0), .in6(1'b1), .in7(1'b0),
    .in8(1'b0), .in9(1'b0), .in10(1'b0), .in11(1'b0), .in12(1'b1), .in13(1'b0), .in14(1'b0), .in15(1'b0),
    .out(multiplexer_1_out), .sel(icode));  // open: en
  Register #(.width(3)) CC_Register (.D({ZF, SF, OF}), .en(multiplexer_1_out), .Q(CC), .clk(Clock), .clr(Reset));
  true_main main_1 (
    .ZF(CC[2]), .SF(CC[1]), .OF(CC[0]), ._0(main_1__0), ._1(main_1__1), ._2(main_1__2), ._3(main_1__3),
    ._4(main_1__4), ._5(main_1__5), ._6(main_1__6), ._7(main_1__7));
  Multiplexer #(.select(4)) multiplexer_2 (
    .in0(main_1__0), .in1(main_1__1), .in2(main_1__2), .in3(main_1__3), .in4(main_1__4), .in5(main_1__5),
    .in6(main_1__6), .in7(main_1__7), .in8(main_1__7), .in9(main_1__7), .in10(main_1__7), .in11(main_1__7),
    .in12(main_1__7), .in13(main_1__7), .in14(main_1__7), .in15(main_1__7), .out(CC_true), .sel(ifun));  // open: en
  and and_1 (and_1_out, ifun[0], ifun[1], ifun[2]);
  or or_1 (invalid_ifun, and_1_out, ifun[3]);
endmodule
