// Logisim project dataselect.circ as structural Verilog: 1 circuit, main circuit dataselect
module dataselect (
  input  [3:0] in_1,
  input  [31:0] ValE_1,
  input  [31:0] ValE_0,
  input  [31:0] ValA_1,
  input  [31:0] ValA_0,
  input  [31:0] ValP_1,
  input  [31:0] ValP_0,
  output [31:0] Addr_1,
  output [31:0] Addr_0,
  output [31:0] Data_1,
  output [31:0] Data_0,
  output read,
  output write
);

  Multiplexer #(.select(4), .width(32)) multiplexer_1 (
    .in0({32{1'b0}}), .in1({32{1'b0}}), .in2({32{1'b0}}), .in3({32{1'b0}}), .in4(ValE_1), .in5(ValE_1),
    .in6({32{1'b0}}), .in7({32{1'b0}}), .in8(ValE_1), .in9(ValA_1), .in10(ValE_1), .in11(ValA_1),
    .in12({32{1'b0}}), .in13({32{1'b0}}), .in14({32{1'b0}}), .in15({32{1'b0}}), .out(Addr_1), .sel(in_1));  // open: en
  Multiplexer #(.select(4), .width(32)) multiplexer_2 (
    .in0({32{1'b0}}), .in1({32{1'b0}}), .in2({32{1'b0}}), .in3({32{1'b0}}), .in4(ValE_0), .in5(ValE_0),
    .in6({32{1'b0}}), .in7({32{1'b0}}), .in8(ValE_0), .in9(ValA_0), .in10(ValE_0), .in11(ValA_0),
    .in12({32{1'b0}}), .in13({32{1'b0}}), .in14({32{1'b0}}), .in15({32{1'b0}}), .out(Addr_0), .sel(in_1));  // open: en
  Multiplexer #(.select(4), .width(32)) multiplexer_3 (
    .in0({32{1'b0}}), .in1({32{1'b0}}), .in2({32{1'b0}}), .in3({32{1'b0}}), .in4(ValA_1), .in5({32{1'b0}}),
    .in6({32{1'b0}}), .in7({32{1'b0}}), .in8(ValP_1), .in9({32{1'b0}}), .in10(ValA_1), .in11({32{1'b0}}),
    .in12({32{1'b0}}), .in13({32{1'b0}}), .in14({32{1'b0}}), .in15({32{1'b0}}), .out(Data_1), .sel(in_1));  // open: en
  Multiplexer #(.select(4), .width(32)) multiplexer_4 (
    .in0({32{1'b0}}), .in1({32{1'b0}}), .in2({32{1'b0}}), .in3({32{1'b0}}), .in4(ValA_0), .in5({32{1'b0}}),
    .in6({32{1'b0}}), .in7({32{1'b0}}), .in8(ValP_0), .in9({32{1'b0}}), .in10(ValA_0), .in11({32{1'b0}}),
    .in12({32{1'b0}}), .in13({32{1'b0}}), .in14({32{1'b0}}), .in15({32{1'b0}}), .out(Data_0), .sel(in_1));  // open: en
  dmemRW dmemrw_1 (.icode(in_1), .read(read), .write(write));
endmodule
