// Logisim project decode.circ as structural Verilog: 1 circuit, main circuit decode
module decode (
  input  [3:0] rA,
  input  [3:0] rB,
  input  [3:0] icode,
  output [3:0] srcA,
  output [3:0] srcB
);

  Multiplexer #(.select(4), .width(4)) multiplexer_1 (
    .in0(4'b1111), .in1(4'b1111), .in2(rA), .in3(4'b1111), .in4(rA), .in5(4'b1111), .in6(rA), .in7(4'b1111),
    .in8(4'b1111), .in9(4'b0100), .in10(rA), .in11(4'b0100), .in12(4'b1111), .in13(4'b1111), .in14(4'b1111),
    .in15(4'b1111), .out(srcA), .sel(icode));  // open: en
  Multiplexer #(.select(4), .width(4)) multiplexer_2 (
    .in0(4'b1111), .in1(4'b1111), .in2(4'b1111), .in3(4'b1111), .in4(rB), .in5(rB), .in6(rB), .in7(4'b1111),
    .in8(4'b0100), .in9(4'b0100), .in10(4'b0100), .in11(4'b0100), .in12(rB), .in13(4'b1111), .in14(4'b1111),
    .in15(4'b1111), .out(srcB), .sel(icode));  // open: en
endmodule
