// Logisim project execute.circ as structural Verilog: 1 circuit, main circuit execute
module execute (
  input  [31:0] valA_1,
  input  [31:0] valA_0,
  input  [31:0] valB_1,
  input  [31:0] valB_0,
  input  [31:0] valC_1,
  input  [31:0] valC_0,
  input  [7:0] icode_ifun,
  output ZF,
  output SF,
  output OF,
  output [31:0] valE_1,
  output [31:0] valE_0
);

  wire [3:0] ifun;
  wire [31:0] aluA_0, aluA_1, aluB_0, aluB_1, bit_extender_1_out;
  wire [31:4] multiplexer_5_out;

  Multiplexer #(.select(4), .width(32), .enable("false")) multiplexer_1 (
    .in0({32{1'b0}}), .in1({32{1'b0}}), .in2(valA_1), .in3(valC_1), .in4(valB_1), .in5(valB_1), .in6(valB_1),
    .in7({32{1'b0}}), .in8(valB_1), .in9(valB_1), .in10(valB_1), .in11(valB_1), .in12(valB_1),
    .in13({32{1'b0}}), .in14({32{1'b0}}), .in15({32{1'b0}}), .out(aluB_1), .sel(icode_ifun[7:4]));
  Multiplexer #(.select(4), .width(32), .enable("false")) multiplexer_2 (
    .in0({32{1'b0}}), .in1({32{1'b0}}), .in2(valA_0), .in3(valC_0), .in4(valB_0), .in5(valB_0), .in6(valB_0),
    .in7({32{1'b0}}), .in8(valB_0), .in9(valB_0), .in10(valB_0), .in11(valB_0), .in12(valB_0),
    .in13({32{1'b0}}), .in14({32{1'b0}}), .in15({32{1'b0}}), .out(aluB_0), .sel(icode_ifun[7:4]));
  Multiplexer #(.select(4), .width(32), .enable("false")) multiplexer_3 (
    .in0({32{1'b0}}), .in1({32{1'b0}}), .in2({32{1'b0}}), .in3({32{1'b0}}), .in4(valC_1), .in5(valC_1),
    .in6(valA_1), .in7({32{1'b0}}), .in8({32{1'b1}}), .in9({32{1'b0}}), .in10({32{1'b1}}), .in11({32{1'b0}}),
    .in12(valC_1), .in13({32{1'b0}}), .in14({32{1'b0}}), .in15({32{1'b0}}), .out(aluA_1),
    .sel(icode_ifun[7:4]));
  Multiplexer #(.select(4), .width(32), .enable("false")) multiplexer_4 (
    .in0({32{1'b0}}), .in1({32{1'b0}}), .in2({32{1'b0}}), .in3({32{1'b0}}), .in4(valC_0), .in5(valC_0),
    .in6(valA_0), .in7({32{1'b0}}), .in8(32'hfffffff8), .in9(32'h8), .in10(32'hfffffff8), .in11(32'h8),
    .in12(valC_0), .in13({32{1'b0}}), .in14({32{1'b0}}), .in15({32{1'b0}}), .out(aluA_0),
    .sel(icode_ifun[7:4]));
  assign bit_extender_1_out = {{28{1'b0}}, icode_ifun[3:0]};  // Bit_Extender bit_extender_1
  // alu alu_1: pin names not known; wires that end beside it: aluA_1, aluA_0, aluB_1, aluB_0, ZF, SF, ifun, OF, valE_1, valE_0
  Multiplexer #(.select(4), .width(32), .enable("false")) multiplexer_5 (
    .in0({32{1'b0}}), .in1({32{1'b0}}), .in2({32{1'b0}}), .in3({32{1'b0}}), .in4({32{1'b0}}),
    .in5({32{1'b0}}), .in6(bit_extender_1_out), .in7({32{1'b0}}), .in8({32{1'b0}}), .in9({32{1'b0}}),
    .in10({32{1'b0}}), .in11({32{1'b0}}), .in12({32{1'b0}}), .in13({32{1'b0}}), .in14({32{1'b0}}),
    .in15({32{1'b0}}), .out({multiplexer_5_out, ifun}), .sel(icode_ifun[7:4]));
  // Probe on ifun

  // Other names for the same wires on the sheet: icode[3:0] = icode_ifun[7:4]
endmodule
