// Logisim project fetch.circ as structural Verilog: 1 circuit, main circuit fetch
module fetch (
  input  [7:0] icode_ifun,
  input  [7:0] rA_rB,
  input  [7:0] in_3,
  input  [7:0] in_4,
  input  [7:0] in_5,
  input  [7:0] in_6,
  input  [7:0] in_7,
  input  [7:0] in_8,
  input  [7:0] in_9,
  input  [7:0] in_10,
  output [3:0] icode,
  output [3:0] ifun,
  output [3:0] rA,
  output [3:0] rB,
  output [31:0] valC_1,
  output [31:0] valC_0
);

  wire multiplexer_1_out;

  Multiplexer #(.select(4)) multiplexer_1 (
    .in0(1'b0), .in1(1'b0), .in2(1'b1), .in3(1'b1), .in4(1'b1), .in5(1'b1), .in6(1'b1), .in7(1'b0),
    .in8(1'b0), .in9(1'b0), .in10(1'b1), .in11(1'b1), .in12(1'b1), .in13(1'b0), .in14(1'b0), .in15(1'b0),
    .out(multiplexer_1_out), .sel(icode_ifun[7:4]));  // open: en
  Multiplexer #(.width(32)) multiplexer_2 (
    .in0({in_9, in_8, in_7, in_6}), .in1({in_10, in_9, in_8, in_7}), .out(valC_1), .sel(multiplexer_1_out));  // open: en
  Multiplexer #(.width(32)) multiplexer_3 (
    .in0({in_5, in_4, in_3, rA_rB}), .in1({in_6, in_5, in_4, in_3}), .out(valC_0), .sel(multiplexer_1_out));  // open: en

  assign icode = icode_ifun[7:4];
  assign ifun = icode_ifun[3:0];
  assign rA = rA_rB[7:4];
  assign rB = rA_rB[3:0];

  // Other names for the same wires on the sheet: valC_N_high[31:0] = {in_9, in_8, in_7, in_6};
  //   valC_R_low[31:0] = {in_6, in_5, in_4, in_3}; valC_R_high[31:0] = {in_10, in_9, in_8, in_7};
  //   valC_N_low[31:0] = {in_5, in_4, in_3, rA_rB}
endmodule
