// Logisim project pcup.circ as structural Verilog: 1 circuit, main circuit PC update
module PC_update (
  input  [31:0] valP,
  input  [31:0] valC,
  input  [31:0] valM,
  input  Cnd,
  input  [3:0] icode,
  output [31:0] PCupdate
);

  wire [31:0] multiplexer_1_out;

  Multiplexer #(.width(32)) multiplexer_1 (.in0(valP), .in1(valC), .out(multiplexer_1_out), .sel(Cnd));  // open: en
  Multiplexer #(.select(4), .width(32)) multiplexer_2 (
    .in0(valP), .in1(valP), .in2(valP), .in3(valP), .in4(valP), .in5(valP), .in6(valP),
    .in7(multiplexer_1_out), .in8(valC), .in9(valM), .in10(valP), .in11(valP), .in12(valP), .in13(valP),
    .in14(valP), .in15(valP), .out(PCupdate), .sel(icode));  // open: en
endmodule
