// Logisim project setvalP.circ as structural Verilog: 1 circuit, main circuit setvalP
module setvalP (
  input  [3:0] icode,
  input  [31:0] PC,
  output [31:0] valP
);

  wire [31:0] multiplexer_1_out;

  Multiplexer #(.select(4), .width(32)) multiplexer_1 (
    .in0(32'h1), .in1(32'h1), .in2(32'h2), .in3(32'ha), .in4(32'ha), .in5(32'ha), .in6(32'h2), .in7(32'h9),
    .in8(32'h9), .in9(32'h1), .in10(32'h2), .in11(32'h2), .in12(32'ha), .in13({32{1'b0}}), .in14({32{1'b0}}),
    .in15({32{1'b0}}), .out(multiplexer_1_out), .sel(icode));  // open: en
  Adder #(.width(32)) adder_1 (.a(multiplexer_1_out), .b(PC), .out(valP));  // open: cin, cout
endmodule
