// Logisim project statU.circ as structural Verilog: 1 circuit, main circuit statU
module statU (
  input  imemErr,
  input  dmemErr,
  input  ifunErr,
  input  [3:0] icode,
  input  [3:0] ifun,
  output [1:0] StatOut
);

  wire multiplexer_2_out, or_3_out;
  wire [2:0] or_1_out;

  Multiplexer #(.select(3), .width(2)) multiplexer_1 (
    .in0(2'b00), .in1(2'b10), .in2(2'b01), .in3(2'b01), .in4(2'b11), .in5(2'b11), .in6(2'b11), .in7(2'b11),
    .out(StatOut), .sel(or_1_out));  // open: en
  or or_1 (or_1_out[0], imemErr, dmemErr);
  or or_2 (or_1_out[1], ifunErr, multiplexer_2_out);
  Multiplexer #(.select(4)) multiplexer_2 (
    .in0(or_3_out), .in1(or_3_out), .in2(1'b0), .in3(or_3_out), .in4(or_3_out), .in5(or_3_out), .in6(1'b0),
    .in7(1'b0), .in8(or_3_out), .in9(or_3_out), .in10(or_3_out), .in11(or_3_out), .in12(or_3_out),
    .in13(1'b1), .in14(1'b1), .in15(1'b1), .out(multiplexer_2_out), .sel(icode));  // open: en
  nor nor_1 (or_1_out[2], icode[0], icode[1], icode[2], icode[3]);
  or or_3 (or_3_out, ifun[3], ifun[2], ifun[1], ifun[0]);
endmodule
