// Logisim project true.circ as structural Verilog: 1 circuit, main circuit main
module main (
  input  ZF,
  input  SF,
  input  OF,
  output _0,
  output _1,
  output _2,
  output _3,
  output _4,
  output _5,
  output _6,
  output _7
);

  xor xor_1 (_2, SF, OF);
  or or_1 (_1, ZF, _2);
  not not_1 (_4, ZF);
  not not_2 (_5, _2);
  and and_1 (_6, _5, _4);

  assign _0 = 1'b1;
  assign _3 = ZF;
  assign _7 = 1'b0;
endmodule
