// Logisim project updateAB.circ as structural Verilog: 1 circuit, main circuit updateAB
module updateAB (
  input  [3:0] rA,
  input  [3:0] rB,
  input  [3:0] icode,
  input  Clock,
  input  Reset,
  output [3:0] rA_2,
  output [3:0] rB_2
);

  wire multiplexer_1_out;

  Multiplexer #(.select(4)) multiplexer_1 (
    .in0(1'b0), .in1(1'b0), .in2(1'b1), .in3(1'b1), .in4(1'b1), .in5(1'b1), .in6(1'b1), .in7(1'b0),
    .in8(1'b0), .in9(1'b0), .in10(1'b1), .in11(1'b1), .in12(1'b0), .in13(1'b0), .in14(1'b0), .in15(1'b0),
    .out(multiplexer_1_out), .sel(icode));  // open: en
  Register register_1 (.D({rB, rA}), .en(multiplexer_1_out), .Q({rB_2, rA_2}), .clk(Clock), .clr(Reset));
endmodule
