// Logisim project y86.circ as structural Verilog: 2 circuits, main circuit main
// execute
module main (
  input  Reset,
  input  Reset_2,
  output [3:0] out_3,
  output [3:0] out_4
);

  wire and_1_out, Clock_out, Cnd, dmemErr, ifunErr, imemErr, nor_1_out, not_1_out, OF, or_1_out, SF, ZF;
  wire [1:0] memRW, Stat_q, statu_1_statout;
  wire [2:0] CC;
  wire [3:0] decode_1_srca, decode_1_srcb, icode, ifun, rA, rB;
  wire [7:0] imem_1_p3, imem_1_p4, imem_1_p5, imem_1_p6, imem_1_p7, imem_1_p8, imem_1_p9, imem_1_p10,
       imem_1_p11, imem_1_p12;
  wire [31:0] dataselect_1_addr_0, dataselect_1_addr_1, dataselect_1_data_0, dataselect_1_data_1, PC_q,
       pc_update_1_pcupdate, PChold_q, valA_0, valA_1, valB_0, valB_1, valC_0, valC_1, valE_0, valE_1,
       valM_0, valM_1, valP;

  and and_1 (and_1_out, Clock_out, nor_1_out);
  Clock Clock (.out(Clock_out));
  Register #(.width(32)) PC (.D(PChold_q), .Q(PC_q), .clk(and_1_out), .clr(Reset));  // open: en
  nor nor_1 (nor_1_out, Stat_q[1], Stat_q[0]);
  setvalP setvalp_1 (.icode(icode), .PC(PC_q), .valP(valP));
  not not_1 (not_1_out, and_1_out);
  Register #(.width(2)) Stat (.D(statu_1_statout), .Q(Stat_q), .clk(not_1_out), .clr(or_1_out));  // open: en
  or or_1 (or_1_out, Reset, Reset_2);
  // imem imem_1: pin names not known; wires that end beside it: PC_q, imemErr, imem_1_p3, imem_1_p4, imem_1_p5, imem_1_p6, imem_1_p7, imem_1_p8, imem_1_p9, imem_1_p10, imem_1_p11, imem_1_p12
  fetch fetch_1 (
    .icode_ifun(imem_1_p3), .rA_rB(imem_1_p4), .in_3(imem_1_p5), .in_4(imem_1_p6), .in_5(imem_1_p7),
    .in_6(imem_1_p8), .in_7(imem_1_p9), .in_8(imem_1_p10), .in_9(imem_1_p11), .in_10(imem_1_p12),
    .icode(icode), .ifun(ifun), .rA(rA), .rB(rB), .valC_1(valC_1), .valC_0(valC_0));
  statU statu_1 (
    .StatOut(statu_1_statout), .imemErr(imemErr), .dmemErr(dmemErr), .ifunErr(ifunErr), .icode(icode),
    .ifun(ifun));
  dst dst_1 (.rA(rA), .rB(rB), .icode(icode), .dstE(out_3), .dstM(out_4));
  decode decode_1 (.rA(rA), .rB(rB), .icode(icode), .srcA(decode_1_srca), .srcB(decode_1_srcb));
  // Probe on icode
  // Probe on ZF
  // Probe on SF
  // Probe on memRW
  // Probe on ifunErr
  // regfile regfile_1: pin names not known; wires that end beside it: decode_1_srca, decode_1_srcb, out_3, valE_1, valE_0, out_4, valM_1, valM_0, not_1_out, Reset, valA_1, valA_0, valB_1, valB_0
  // Probe on ifun
  // Probe on CC
  // Probe on OF
  // Probe on dmemErr
  // Probe on rA
  // Probe on rB
  // Probe on Cnd
  // Probe on imemErr
  execute execute_1 (
    .valA_1(valA_1), .valA_0(valA_0), .valB_1(valB_1), .valB_0(valB_0), .valC_1(valC_1), .valC_0(valC_0),
    .ZF(ZF), .SF(SF), .OF(OF), .icode_ifun({icode, ifun}), .valE_1(valE_1), .valE_0(valE_0));
  // Probe on valC_0
  // Probe on valE_1
  // Probe on valC_1
  // Probe on valE_0
  CC cc_1 (
    .icode(icode), .ifun(ifun), .CC(CC), .Clock(not_1_out), .Reset(Reset), .ZF(ZF), .SF(SF), .OF(OF),
    .CC_true(Cnd), .invalid_ifun(ifunErr));
  // Probe on valP
  // Probe on valM_1
  dataselect dataselect_1 (
    .in_1(icode), .ValE_1(valE_1), .ValE_0(valE_0), .ValA_1(valA_1), .ValA_0(valA_0), .ValP_1({32{1'b0}}),
    .ValP_0(valP), .Addr_1(dataselect_1_addr_1), .Addr_0(dataselect_1_addr_0), .Data_1(dataselect_1_data_1),
    .Data_0(dataselect_1_data_0), .read(memRW[1]), .write(memRW[0]));
  // Probe on valA_1
  // Probe on valM_0
  PC_update pc_update_1 (
    .valP(valP), .valC(valC_0), .valM(valM_0), .Cnd(Cnd), .icode(icode), .PCupdate(pc_update_1_pcupdate));
  // dmem dmem_1: pin names not known; wires that end beside it: dataselect_1_addr_1, dataselect_1_addr_0, dataselect_1_data_1, dataselect_1_data_0, memRW[1], memRW[0], dmemErr, not_1_out, Reset, valM_1, valM_0
  // Probe on valA_0
  // Probe on valB_1
  // Probe on valB_0
  Register #(.width(32)) PChold (.D(pc_update_1_pcupdate), .en(1'b1), .Q(PChold_q), .clk(not_1_out), .clr(Reset));

  // Other names for the same wires on the sheet: dstE[3:0] = out_3; dstM[3:0] = out_4
endmodule

module Align (
  input  [7:0] B1,
  input  [7:0] B2,
  input  [7:0] B3,
  input  [7:0] B4,
  input  [7:0] B5,
  input  [7:0] B6,
  input  [7:0] B7,
  input  [7:0] B8,
  input  [7:0] B9,
  input  NeedRegs,
  output [3:0] rA,
  output [3:0] rB,
  output [31:0] valC_1,
  output [31:0] valC_0
);
endmodule
